# Fritzing sketch Smart Parking System Complete w Camera (saved by Fritzing 0.9.3b)
breadboards: 1

parts:
  LED1 = LED - 5mm [color="Red (633nm)" package="5 mm [THT]"]
  LED2 = LED - 5mm [color="Red (633nm)" package="5 mm [THT]"]
  LED4 = LED - 5mm [color="Green (555nm)" package="5 mm [THT]"]
  LED5 = LED - 5mm [color="Yellow (595nm)" package="5 mm [THT]"]
  LED6 = LED - 5mm [color="Green (555nm)" package="5 mm [THT]"]
  HC-SR04_Sensor_1 = HC-SR04 Ultrasonic Distance Sensor
  HC-SR04_Sensor_2 = HC-SR04 Ultrasonic Distance Sensor
  HC-SR04_Sensor_3 = HC-SR04 Ultrasonic Distance Sensor
  R1 = Resistor [tolerance=±5% resistance=1k package="2512 [SMD]"]
  R2 = Resistor [tolerance=±5% resistance=1k package="2512 [SMD]"]
  R3 = Resistor [tolerance=±5% resistance=1k package="2512 [SMD]"]
  R4 = Resistor [tolerance=±5% resistance=1k package="2512 [SMD]"]
  R5 = Resistor [tolerance=±5% resistance=1k package="2512 [SMD]"]
  R6 = Resistor [tolerance=±5% resistance=1k package="2512 [SMD]"]
  R7 = Resistor [tolerance=±5% resistance=1k package="2512 [SMD]"]
  R8 = Resistor [tolerance=±5% resistance=1k package="2512 [SMD]"]
  R9 = Resistor [tolerance=±5% resistance=1k package="2512 [SMD]"]
  R10 = Resistor [tolerance=±5% resistance=330 package="2512 [SMD]"]
  R11 = Resistor [tolerance=±5% resistance=330 package="2512 [SMD]"]
  R12 = Resistor [tolerance=±5% resistance=330 package="2512 [SMD]"]
  R13 = Resistor [tolerance=±5% resistance=330 package="2512 [SMD]"]
  R14 = Resistor [tolerance=±5% resistance=330 package="2512 [SMD]"]
  R15 = Resistor [tolerance=±5% resistance=330 package="2512 [SMD]"]
  Potentiometer_1 = Rotary Potentiometer (Small) [maximum_resistance=10kΩ package=THT]
  LED3 = LED - 5mm [color="Red (633nm)" package="5 mm [THT]"]
  Raspberry_Pi = Raspberry Pi 3 [part_number=RPI-3-V1.2]
  LCD_Display_1 = LCD-16X2 [package=lcd-16x2]
  U1 = TRANSCHIPTC5747 [package=camera_sfv24r-2st_2]

nets:
  N1: LED1.cathode, R15.Pin_0
  N2: LED1.anode, Raspberry_Pi.GPIO15
  N3: LED2.cathode, R12.Pin_0
  N4: LED2.anode, Raspberry_Pi.GPIO4
  N5: LED4.cathode, R13.Pin_0
  N6: LED4.anode, Raspberry_Pi.GPIO14, U1.DOUT_4
  N7: LED5.cathode, R11.Pin_0
  N8: LED5.anode, Raspberry_Pi.GPIO3
  N9: LED6.cathode, R14.Pin_0
  N10: LED6.anode, Raspberry_Pi.GPIO18
  VCC: HC-SR04_Sensor_1.VCC, HC-SR04_Sensor_2.VCC, HC-SR04_Sensor_3.VCC, Potentiometer_1.leg1, Raspberry_Pi.5V, LCD_Display_1.VDD, LCD_Display_1.A, U1.VALIDV
  N11: HC-SR04_Sensor_1.TRIG, Raspberry_Pi.GPIO17
  N12: HC-SR04_Sensor_1.ECHO, R5.Pin_0
  GND: HC-SR04_Sensor_1.GND, HC-SR04_Sensor_2.GND, HC-SR04_Sensor_3.GND, R2.Pin_0, R8.Pin_0, R9.Pin_0, R10.Pin_1, R11.Pin_1, R12.Pin_1, R13.Pin_1, R14.Pin_1, R15.Pin_1, Potentiometer_1.leg2, Raspberry_Pi.GND, LCD_Display_1.VSS, LCD_Display_1.R_W, LCD_Display_1.K
  N13: HC-SR04_Sensor_2.TRIG, Raspberry_Pi.GPIO22
  N14: HC-SR04_Sensor_2.ECHO, R6.Pin_0
  N15: HC-SR04_Sensor_3.TRIG, Raspberry_Pi.GPIO27
  N16: HC-SR04_Sensor_3.ECHO, R1.Pin_0
  N17: R1.Pin_1, R7.Pin_1, Raspberry_Pi.GPIO24
  N18: R2.Pin_1, R3.Pin_0
  N19: R3.Pin_1, R5.Pin_1, Raspberry_Pi.GPIO23
  N20: R4.Pin_0, R9.Pin_1
  N21: R4.Pin_1, R6.Pin_1, Raspberry_Pi.GPIO10
  N22: R7.Pin_0, R8.Pin_1
  N23: R10.Pin_0, LED3.cathode
  N24: Potentiometer_1.wiper, LCD_Display_1.VO
  N25: LED3.anode, Raspberry_Pi.GPIO2
  N26: Raspberry_Pi.3v3, U1.DVDD28
  N27: Raspberry_Pi.GPIO9, LCD_Display_1.E
  N28: Raspberry_Pi.GPIO11, LCD_Display_1.DB4, U1.AVDD28, U1.DGND
  N29: Raspberry_Pi.GPIO5, LCD_Display_1.DB5
  N30: Raspberry_Pi.GPIO6, LCD_Display_1.DB6
  N31: Raspberry_Pi.GPIO13, LCD_Display_1.DB7
  N32: Raspberry_Pi.GPIO25, LCD_Display_1.RS
