# Fritzing sketch Smart Parking System LEDs first (saved by Fritzing 0.9.3b)
breadboards: 1

parts:
  LED1 = LED - 5mm [color="Red (633nm)" package="5 mm [THT]"]
  LED2 = LED - 5mm [color="Red (633nm)" package="5 mm [THT]"]
  LED4 = LED - 5mm [color="Green (555nm)" package="5 mm [THT]"]
  LED5 = LED - 5mm [color="Yellow (595nm)" package="5 mm [THT]"]
  LED6 = LED - 5mm [color="Green (555nm)" package="5 mm [THT]"]
  HC-SR04_Sensor_1 = HC-SR04 Ultrasonic Distance Sensor
  HC-SR04_Sensor_2 = HC-SR04 Ultrasonic Distance Sensor
  HC-SR04_Sensor_3 = HC-SR04 Ultrasonic Distance Sensor
  LCD_Display_1 = LCD-16X2 [package=lcd-16x2_noholes]  # not connected
  R1 = Resistor [tolerance=±5% resistance=1k package="2512 [SMD]"]  # not connected
  R2 = Resistor [tolerance=±5% resistance=1k package="2512 [SMD]"]  # not connected
  R3 = Resistor [tolerance=±5% resistance=1k package="2512 [SMD]"]  # not connected
  R4 = Resistor [tolerance=±5% resistance=1k package="2512 [SMD]"]  # not connected
  R5 = Resistor [tolerance=±5% resistance=1k package="2512 [SMD]"]  # not connected
  R6 = Resistor [tolerance=±5% resistance=1k package="2512 [SMD]"]  # not connected
  R7 = Resistor [tolerance=±5% resistance=1k package="2512 [SMD]"]  # not connected
  R8 = Resistor [tolerance=±5% resistance=1k package="2512 [SMD]"]  # not connected
  R9 = Resistor [tolerance=±5% resistance=1k package="2512 [SMD]"]  # not connected
  R10 = Resistor [tolerance=±5% resistance=330 package="2512 [SMD]"]
  R11 = Resistor [tolerance=±5% resistance=330 package="2512 [SMD]"]
  R12 = Resistor [tolerance=±5% resistance=330 package="2512 [SMD]"]
  R13 = Resistor [tolerance=±5% resistance=330 package="2512 [SMD]"]
  R14 = Resistor [tolerance=±5% resistance=330 package="2512 [SMD]"]
  R15 = Resistor [tolerance=±5% resistance=330 package="2512 [SMD]"]
  Potentiometer_1 = Rotary Potentiometer (Small) [maximum_resistance=10kΩ package=THT]  # not connected
  LED3 = LED - 5mm [color="Red (633nm)" package="5 mm [THT]"]
  Raspberry_Pi = Raspberry Pi 3 [part_number=RPI-3-V1.2]

nets:
  N1: LED1.cathode, Raspberry_Pi.GPIO15
  N2: LED1.anode, R15.Pin_0
  N3: LED2.cathode, Raspberry_Pi.GPIO4
  N4: LED2.anode, R12.Pin_0
  N5: LED4.cathode, Raspberry_Pi.GPIO14
  N6: LED4.anode, R13.Pin_0
  N7: LED5.cathode, Raspberry_Pi.GPIO3
  N8: LED5.anode, R11.Pin_0
  N9: LED6.cathode, Raspberry_Pi.GPIO18
  N10: LED6.anode, R14.Pin_0
  VCC: HC-SR04_Sensor_1.VCC, HC-SR04_Sensor_2.VCC, HC-SR04_Sensor_3.VCC, Raspberry_Pi.5V
  N11: R10.Pin_0, LED3.anode
  N12: R10.Pin_1, R11.Pin_1, R12.Pin_1, R13.Pin_1, R14.Pin_1, R15.Pin_1, Raspberry_Pi.GND
  N13: LED3.cathode, Raspberry_Pi.GPIO2
